# Fritzing sketch LEDLight (saved by Fritzing 0.9.2b)
breadboards: 1

parts:
  Part1 = Arduino Uno (Rev3)
  LED1 = RGB LED (com. anode, rbg) [package="5 mm [THT]"]
  S1 = Pushbutton [package="[SMD]"]
  R1 = Resistor [tolerance=±5% resistance=220 package=THT]
  R2 = Resistor [tolerance=±5% resistance=220 package=THT]
  R3 = Resistor [tolerance=±5% resistance=220 package=THT]
  R4 = Resistor [tolerance=±5% resistance=220 package=THT]

nets:
  N1: Part1.D9_PWM, R4.Pin_1
  N2: Part1.D10_PWM/SS, R3.Pin_1
  N3: Part1.D11_PWM/MOSI, R2.Pin_1
  N4: Part1.D13/SCK, S1.Pin_1, S1.Pin_2, R1.Pin_0
  N5: Part1.GND, S1.Pin_3, S1.Pin_4
  N6: Part1.5V, LED1.blue_cathode, R1.Pin_1
  N7: LED1.red_cathode, R2.Pin_0
  N8: LED1.common_anode, R3.Pin_0
  N9: LED1.green_cathode, R4.Pin_0
