# Fritzing sketch HBridge (saved by Fritzing 0.9.2b)
breadboards: 1

parts:
  IC1 = H-Bridge [package=THT]
  M1 = DC Motor
  M2 = DC Motor
  J1 = Generic female header - 2 pins [form="♀ (female)" package=THT]  # not connected
  Part1 = Arduino Uno (Rev3)

nets:
  N1: IC1.1_2EN, Part1.D11_PWM/MOSI
  N2: IC1.1A, Part1.D5_PWM
  N3: IC1.1Y, M2.pin_2
  GND2: IC1.GND2, IC1.GND4, Part1.GND
  N4: IC1.2Y, M2.pin_1
  N5: IC1.2A, Part1.D4
  N6: IC1.VCC2, IC1.VCC1, Part1.5V
  N7: IC1.3_4EN, Part1.D10_PWM/SS
  N8: IC1.3A, Part1.D2
  N9: IC1.3Y, M1.pin_2
  N10: IC1.4Y, M1.pin_1
  N11: IC1.4A, Part1.D3_PWM

custom parts:
  Generic female header - 2 pins: Generic female header
