# Fritzing sketch Flag (saved by Fritzing 0.9.2b)
breadboards: 1

parts:
  Part1 = Arduino Uno (Rev3) - ICSP
  LED1 = RGB LED (com. anode, rbg) [package="5 mm [THT]"]
  LED2 = LED - 3mm [color="Red (633nm)" package="3 mm [THT]"]
  LED3 = LED - 3mm [color="Red (633nm)" package="3 mm [THT]"]
  LED4 = LED - 3mm [color="Red (633nm)" package="3 mm [THT]"]
  R1 = Resistor [tolerance=±5% resistance=220 package=THT]
  R2 = Resistor [tolerance=±5% resistance=220 package=THT]
  R3 = Resistor [tolerance=±5% resistance=220 package=THT]
  R4 = Resistor [tolerance=±5% resistance=220 package=THT]
  R5 = Resistor [tolerance=±5% resistance=220 package=THT]
  R6 = Resistor [tolerance=±5% resistance=220 package=THT]

nets:
  N1: Part1.ICSP_MISO, Part1.D12/MISO, LED3.anode
  N2: Part1.ICSP_MOSI, Part1.D11_PWM/MOSI, LED4.anode
  N3: Part1.D13/SCK, LED2.anode
  N4: Part1.GND, R4.Pin_1, R5.Pin_1, R6.Pin_1
  N5: Part1.D1/TX, R1.Pin_1
  N6: Part1.D2, R2.Pin_1
  N7: Part1.D3_PWM, R3.Pin_1
  N8: Part1.5V, LED1.blue_cathode
  N9: LED1.red_cathode, R3.Pin_0
  N10: LED1.common_anode, R2.Pin_0
  N11: LED1.green_cathode, R1.Pin_0
  N12: LED2.cathode, R4.Pin_0
  N13: LED3.cathode, R5.Pin_0
  N14: LED4.cathode, R6.Pin_0
